# Fritzing sketch plantes (saved by Fritzing 0.9.3b)
circuit board: 8.46667cm x 5.64444cm
breadboards: 1

parts:
  Tiny_RTC1 = Tiny RTC
  Arduino = Arduino Pro Mini (5V)
  FET1 = Basic FET N-Channel [part_number="FQP 30N06L" package="TO220 [THT]"]
  IC1 = Voltage Regulator [package=to220-igo]
  FET2 = Basic FET N-Channel [part_number="FQP 30N06L" package="TO220 [THT]"]
  FET3 = Basic FET N-Channel [part_number="FQP 30N06L" package="TO220 [THT]"]
  M1 = DC Motor [part_number=12VCC]
  M2 = DC Motor [part_number=12VCC]
  M3 = DC Motor [part_number=12VCC]
  LED1 = LED - 5mm [color="Red (633nm)" package="5 mm [THT]"]
  D1 = Rectifier Diode [part_number=1N4001 package="300 mil [THT]"]
  C1 = Ceramic Capacitor [capacitance=100nF package="200 mil [THT, multilayer]"]
  C2 = Ceramic Capacitor [capacitance=100nF package="200 mil [THT, multilayer]"]
  C3 = Ceramic Capacitor [capacitance=100nF package="200 mil [THT, multilayer]"]
  R1 = Resistor [tolerance=±5% resistance=10k package=THT]
  R2 = Resistor [tolerance=±5% resistance=10k package=THT]
  R3 = Resistor [tolerance=±5% resistance=10k package=THT]
  D2 = Rectifier Diode [part_number=1N4001 package="300 mil [THT]"]
  D3 = Rectifier Diode [part_number=1N4001 package="300 mil [THT]"]
  R4 = Resistor [tolerance=±5% resistance=220 package=THT]
  R5 = Resistor [tolerance=±5% resistance=220 package=THT]
  LED2 = LED - 5mm [color="Red (633nm)" package="5 mm [THT]"]
  LED3 = LED - 5mm [color="Red (633nm)" package="5 mm [THT]"]
  R6 = Resistor [tolerance=±5% resistance=220 package=THT]
  J1 = Power Jack [part_number=12V package=power_jack_slot]

nets:
  N1: Tiny_RTC1.SCL, Arduino.A5
  N2: Tiny_RTC1.SDA, Arduino.A4
  VCC: Tiny_RTC1.VCC, Arduino.VCC, IC1.OUT
  GND: Tiny_RTC1.GND#4, Arduino.GND, FET1.source, IC1.GND, FET2.source, FET3.source, R1.Pin_1, R2.Pin_1, R3.Pin_1, R4.Pin_1, R5.Pin_1, R6.Pin_1, J1.GND
  N3: Arduino.D9, FET3.gate, R3.Pin_0, LED3.anode
  N4: Arduino.D5, FET2.gate, R2.Pin_0, LED2.anode
  N5: Arduino.D4, FET1.gate, LED1.anode, R1.Pin_0
  N6: FET1.drain, M1.pin_2, D1.anode, C1.0
  N7: IC1.IN, M1.pin_1, M2.pin_1, M3.pin_1, D1.cathode, C1.1, C2.1, C3.1, D2.cathode, D3.cathode, J1.PWR
  N8: FET2.drain, M2.pin_2, C2.0, D2.anode
  N9: FET3.drain, M3.pin_2, C3.0, D3.anode
  N10: LED1.cathode, R4.Pin_0
  N11: R5.Pin_0, LED2.cathode
  N12: LED3.cathode, R6.Pin_0

custom parts:
  Tiny RTC: Tiny RTC I2C module DS1370Z RTC and AT24C32 EEPROM
